// Logisim project tp1.circ as structural Verilog
module demi_add (
  input  A,
  input  B,
  output S,
  output R
);

  and and_1 (R, A, B);
  xor xor_1 (S, A, B);
endmodule

module add1 (
  input  B,
  input  A,
  input  Re,
  output Rs,
  output S
);

  wire demi_add_1_r, demi_add_1_s, demi_add_2_r;

  demi_add demi_add_1 (.A(A), .B(B), .R(demi_add_1_r), .S(demi_add_1_s));
  or or_1 (Rs, demi_add_1_r, demi_add_2_r);
  demi_add demi_add_2 (.A(Re), .B(demi_add_1_s), .R(demi_add_2_r), .S(S));
endmodule

module add4 (
  input  B3,
  input  A3,
  input  B2,
  input  A2,
  input  B1,
  input  A1,
  input  B0,
  input  A0,
  input  Re,
  output Rs,
  output S3,
  output S2,
  output S1,
  output S0
);

  wire add1_2_rs, add1_3_rs, add1_4_rs;

  add1 add1_1 (.B(B3), .A(A3), .Re(add1_2_rs), .Rs(Rs), .S(S3));
  add1 add1_2 (.B(B2), .A(A2), .Re(add1_3_rs), .Rs(add1_2_rs), .S(S2));
  add1 add1_3 (.B(B1), .A(A1), .Re(add1_4_rs), .Rs(add1_3_rs), .S(S1));
  add1 add1_4 (.B(B0), .A(A0), .Re(Re), .Rs(add1_4_rs), .S(S0));
endmodule

module multi (
  input  a3,
  input  a2,
  input  a1,
  input  a0,
  input  b1,
  input  b0,
  output [5:0] out_7
);

  wire add1_1_rs, add1_2_rs, demi_add_1_r, x1_out, x2_out, x3_out, y0_out, y1_out, y2_out, y3_out;

  and x0 (out_7[0], b0, a0);
  and x1 (x1_out, b0, a1);
  and x2 (x2_out, b0, a2);
  and x3 (x3_out, b0, a3);
  and y0 (y0_out, b1, a0);
  and y1 (y1_out, b1, a1);
  and y2 (y2_out, b1, a2);
  and y3 (y3_out, b1, a3);
  demi_add demi_add_1 (.A(x1_out), .B(y0_out), .R(demi_add_1_r), .S(out_7[1]));
  add1 add1_1 (.B(y1_out), .A(x2_out), .Re(demi_add_1_r), .Rs(add1_1_rs), .S(out_7[2]));
  add1 add1_2 (.B(y2_out), .A(x3_out), .Re(add1_1_rs), .Rs(add1_2_rs), .S(out_7[3]));
  demi_add demi_add_2 (.A(add1_2_rs), .B(y3_out), .R(out_7[5]), .S(out_7[4]));
endmodule

module UAL (
  input  [3:0] A,
  input  [3:0] B,
  input  [2:0] Op,
  output [3:0] out_4,
  output [5:0] out_5,
  output Cin,
  output out_7
);

  wire not_1_out, not_2_out, not_3_out, not_4_out;
  wire [3:0] undriven;

  add4 add4_1 (
    .B3(B[3]), .A3(A[3]), .B2(B[2]), .A2(A[2]), .B1(B[1]), .A1(A[1]), .B0(B[0]), .A0(A[0]), .Re(Cin));  // open: Rs, S3, S2, S1, S0
  not not_1 (not_1_out, B[3]);
  not not_2 (not_2_out, B[2]);
  not not_3 (not_3_out, B[0]);
  not not_4 (not_4_out, B[1]);
  add4 add4_2 (
    .B3(not_1_out), .A3(A[3]), .B2(not_2_out), .A2(A[2]), .B1(not_4_out), .A1(A[1]), .B0(not_3_out),
    .A0(A[0]), .Re(out_7));  // open: Rs, S3, S2, S1, S0
  multi multi_1 (.a3(A[3]), .a2(A[2]), .a1(A[1]), .a0(A[0]), .b1(B[1]), .b0(B[0]), .out_7(out_5));
  Multiplexer #(.select(4)) multiplexer_1 (.sel(undriven));  // open: in0, in1, in2, in3, in4, in5, in6, in7, in8, in9, in10, in11, in12, in13, in14, in15, out, en
  not not_5 (out_4[0], A[0]);
  not not_6 (out_4[1], A[1]);
  not not_7 (out_4[3], A[3]);
  not not_8 (out_4[2], A[2]);
endmodule
